# Fritzing sketch StormCandleBasic (saved by Fritzing 0.9.3b)
breadboards: 1

parts:
  Composant1 = Arduino Nano (Rev3.0)
  LED1 = DUO LED RG [package="5 mm [THT]"]
  R1 = Resistor [tolerance=±5% resistance=220 package=THT]
  R2 = Resistor [tolerance=±5% resistance=220 package=THT]
  Composant2 = Barometric Pressure Sensor - BMP180 Breakout (GY-68)
  S1 = Toggle Switch [package=THT]
  R3 = Resistor [tolerance=±5% resistance=220 package="1206 [SMD]"]
  R4 = PHOTOCELL [package=photocell]
  S2 = Momentary Switch [package=ksa_sealed_tac_switch]

nets:
  N1: Composant1.D5, R2.Pin_0
  N2: Composant1.D6, R1.Pin_0
  N3: Composant1.D7, S1.L2
  N4: Composant1.D8, S1.L1
  N5: Composant1.D12/MISO, S2.2
  GND: Composant1.GND, LED1.common_cathode, Composant2.GND, S1.COM, R3.Pin_1, S2.1
  5V: Composant1.5V, Composant2.VCC, R4.P$1
  N6: Composant1.A6, R3.Pin_0, R4.P$2
  N7: Composant1.A5, Composant2.SCL
  N8: Composant1.A4, Composant2.SDA
  N9: LED1.red_anode, R1.Pin_1
  N10: LED1.green_anode, R2.Pin_1

notes:
  BMP180
  A4 = SDA, A5 = SCL
  Three-way switch
  D7 = Auto brightness
  D8 = Full brightness
  None = LED off
  EEPROM reset button
